# Fritzing sketch xmasfish (saved by Fritzing 0.9.3b)
breadboards: 1

parts:
  DFRobot_DFPlayer_Mini1 = DFRobot DFPlayer Mini [part_number=DFR0299]
  Part1 = Arduino Nano (Rev3.0)
  J1 = Piezo Speaker
  R1 = Resistor [tolerance=±5% resistance=220 package="2010 [SMD]"]
  S3 = Pushbutton [package="[SMD]"]
  S4 = Momentary Switch [package=ksa_sealed_tac_switch]
  S5 = Pushbutton [package="[SMD]"]

nets:
  VCC: DFRobot_DFPlayer_Mini1.VCC, Part1.5V
  N1: DFRobot_DFPlayer_Mini1.TX, Part1.D10
  N2: DFRobot_DFPlayer_Mini1.SPK_1, J1.pin2
  N3: DFRobot_DFPlayer_Mini1.GND-1, DFRobot_DFPlayer_Mini1.GND-2, Part1.GND
  N4: DFRobot_DFPlayer_Mini1.SPK_2, J1.pin1
  N5: Part1.D2, S5.Pin_1, S5.Pin_2
  N6: Part1.D3, S3.Pin_1, S3.Pin_2
  N7: Part1.D4, S4.1
  N8: Part1.D11/MOSI, R1.Pin_1
